// Logisim project newcpu.circ as structural Verilog: 5 circuits, main circuit main
// RESET
module main (
  input  [7:0] in_1
);

  wire button_1_out, button_2_out, button_3_out, clDISP, clDISPLATCH, CLK, clWOUT, d1, d2, d3, d4, d_ff_1_q,
       nCLK, uRESET;
  wire [3:0] s1h, s1l, s2h, s2l, s3h, s3l, s4h, s4l;
  wire [7:0] register_1_q, segdisplay_1_hseg;

  Button button_1 (.out(button_1_out));
  Button button_2 (.out(button_2_out));
  Clock clock_1 (.out(CLK));
  not not_1 (nCLK, CLK);
  debounce debounce_1 (.resp(clWOUT), .req(button_1_out), .clk(CLK));
  LED led_1 (.in(clWOUT));
  debounce debounce_2 (.resp(uRESET), .req(button_2_out), .clk(CLK));
  LED led_2 (.in(uRESET));
  D_Flip_Flop d_ff_1 (.D(clDISP), .clk(clDISPLATCH), .Q(d_ff_1_q), .reset(uRESET));  // open: Qn, preset
  Register register_1 (.D(in_1), .en(clWOUT), .clk(CLK), .Q(register_1_q), .clr(uRESET));
  _7_Segment_Display digit4 (
    .g(s4h[3]), .f(s4h[2]), .a(s4h[1]), .b(s4h[0]), .e(s4l[3]), .d(s4l[2]), .c(s4l[1]), .dp(s4l[0]));
  Button button_3 (.out(button_3_out));
  _7_Segment_Display digit3 (
    .g(s3h[3]), .f(s3h[2]), .a(s3h[1]), .b(s3h[0]), .e(s3l[3]), .d(s3l[2]), .c(s3l[1]), .dp(s3l[0]));
  _7_Segment_Display digit2 (
    .g(s2h[3]), .f(s2h[2]), .a(s2h[1]), .b(s2h[0]), .e(s2l[3]), .d(s2l[2]), .c(s2l[1]), .dp(s2l[0]));
  toggleswitch toggleswitch_1 (.switch(clDISP), .latch(clDISPLATCH), .clk(CLK), .res(uRESET), .I(button_3_out));
  _7_Segment_Display digit1 (
    .g(s1h[3]), .f(s1h[2]), .a(s1h[1]), .b(s1h[0]), .e(s1l[3]), .d(s1l[2]), .c(s1l[1]), .dp(s1l[0]));
  LED led_3 (.in(clDISP));
  segdisplay segdisplay_1 (
    .reset(uRESET), .clk(CLK), .value(register_1_q), .sign(1'b0), .en(d_ff_1_q), .anode({d4, d3, d2, d1}),
    .hseg(segdisplay_1_hseg));
  assign {s1h, s1l} = d1 ? segdisplay_1_hseg : 8'bz;  // Controlled_Buffer controlled_buffer_1
  assign {s2h, s2l} = d2 ? segdisplay_1_hseg : 8'bz;  // Controlled_Buffer controlled_buffer_2
  assign {s3h, s3l} = d3 ? segdisplay_1_hseg : 8'bz;  // Controlled_Buffer controlled_buffer_3
  assign {s4h, s4l} = d4 ? segdisplay_1_hseg : 8'bz;  // Controlled_Buffer controlled_buffer_4

  // Other names for the same wires on the sheet: DBUS[7:0] = in_1; fCLK = CLK

  // Notes on the sheet:
  //   OUTPUT REGISTER
endmodule

module ring (
  input  clr,
  input  clk,
  output [3:0] Q
);

  wire q4, q5, q6, q7;

  D_Flip_Flop d_ff_1 (.D(q6), .clk(clk), .Q(q7), .reset(clr));  // open: Qn, preset
  D_Flip_Flop d_ff_2 (.D(q5), .clk(clk), .Q(q6), .reset(clr));  // open: Qn, preset
  D_Flip_Flop d_ff_3 (.D(q4), .clk(clk), .Q(q5), .reset(clr));  // open: Qn, preset
  D_Flip_Flop d_ff_4 (.D(Q[3]), .clk(clk), .Q(q4), .reset(clr));  // open: Qn, preset
  D_Flip_Flop d_ff_5 (.D(Q[2]), .clk(clk), .Q(Q[3]), .reset(clr));  // open: Qn, preset
  D_Flip_Flop d_ff_6 (.D(Q[1]), .clk(clk), .Q(Q[2]), .reset(clr));  // open: Qn, preset
  D_Flip_Flop d_ff_7 (.D(Q[0]), .clk(clk), .Q(Q[1]), .reset(clr));  // open: Qn, preset
  D_Flip_Flop d_ff_8 (.D(Q[3]), .clk(clk), .Q(Q[0]), .preset(clr));  // open: Qn, reset
endmodule

module segdisplay (
  input  reset,
  input  clk,
  input  [7:0] value,
  input  sign,
  input  en,
  output [3:0] anode,
  output [7:0] hseg
);

  wire wclk;
  wire [3:0] register_1_q, ring_1_p3;
  wire [7:0] register_2_q, SEGROM_data;

  not not_1 (wclk, clk);
  ROM #(.addrWidth(13)) SEGROM (.addr({1'b0, ring_1_p3, value}), .data(SEGROM_data));
  // ring ring_1: pin names not known; wires that end beside it: reset, clk, ring_1_p3
  Register #(.width(4)) register_1 (.D(ring_1_p3), .en(en), .clk(wclk), .Q(register_1_q));  // open: clr
  Register register_2 (.D(SEGROM_data), .en(en), .clk(wclk), .Q(register_2_q));  // open: clr
  assign anode = en ? register_1_q : 4'bz;  // Controlled_Buffer controlled_buffer_1
  assign hseg = en ? register_2_q : 8'bz;  // Controlled_Buffer controlled_buffer_2

  // Other names for the same wires on the sheet: clr = reset; sgn = sign

  // Notes on the sheet:
  //   contents of SEGROM (hex, n*v repeats v):
  //   256*0 7e 12 bc b6 d2 e6 ee 32 fe f2 7e 12 bc b6 d2 e6 ee 32 fe f2 7e 12 bc b6 d2 e6 ee 32 fe f2 7e
  //   12 bc b6 d2 e6 ee 32 fe f2 7e 12 bc b6 d2 e6 ee 32 fe f2 7e 12 bc b6 d2 e6 ee 32 fe f2 7e 12 bc b6
  //   d2 e6 ee 32 fe f2 7e 12 bc b6 d2 e6 ee 32 fe f2 7e 12 bc b6 d2 e6 ee 32 fe f2 7e 12 bc b6 d2 e6 ee
  //   32 fe f2 7e 12 bc b6 d2 e6 ee 32 fe f2 7e 12 bc b6 d2 e6 ee 32 fe f2 7e 12 bc b6 d2 e6 ee 32 fe f2
  //   7e 12 bc b6 d2 e6 ee 32 fe f2 7e 12 bc b6 d2 e6 ee 32 fe f2 7e 12 bc b6 d2 e6 ee 32 fe f2 7e 12 bc
  //   b6 d2 e6 ee 32 fe f2 7e 12 bc b6 d2 e6 ee 32 fe f2 7e 12 bc b6 d2 e6 ee 32 fe f2 7e 12 bc b6 d2 e6
  //   ee 32 fe f2 7e 12 bc b6 d2 e6 ee 32 fe f2 7e 12 bc b6 d2 e6 ee 32 fe f2 7e 12 bc b6 d2 e6 ee 32 fe
  //   f2 7e 12 bc b6 d2 e6 ee 32 fe f2 7e 12 bc b6 d2 e6 ee 32 fe f2 7e 12 bc b6 d2 e6 10*0 10*12 10*bc
  //   10*b6 10*d2 10*e6 10*ee 10*32 10*fe 10*f2 10*7e 10*12 10*bc 10*b6 10*d2 10*e6 10*ee 10*32 10*fe
  //   10*f2 10*7e 10*12 10*bc 10*b6 10*d2 6*e6 6*1 10*ff 340*0 100*12 56*bc
endmodule

module debounce (
  input  req,
  input  clk,
  output resp
);

  wire d_ff_1_q, d_ff_1_qn, d_ff_2_qn;

  D_Flip_Flop d_ff_1 (.D(req), .clk(clk), .Q(d_ff_1_q), .Qn(d_ff_1_qn));  // open: preset, reset
  D_Flip_Flop d_ff_2 (.D(d_ff_1_q), .clk(clk), .Qn(d_ff_2_qn));  // open: Q, preset, reset
  D_Flip_Flop d_ff_3 (.D(d_ff_2_qn), .clk(clk), .Qn(resp));  // open: Q, preset, reset
endmodule

module toggleswitch (
  input  I,
  input  clk,
  input  res,
  output switch,
  output latch
);

  wire d_ff_1_q, d_ff_2_qn;

  D_Flip_Flop d_ff_1 (.D(I), .clk(clk), .Q(d_ff_1_q), .reset(res));  // open: Qn, preset
  D_Flip_Flop d_ff_2 (.D(d_ff_2_qn), .clk(d_ff_1_q), .Q(switch), .Qn(d_ff_2_qn), .reset(res));  // open: preset
  D_Flip_Flop d_ff_3 (.D(d_ff_1_q), .clk(clk), .Q(latch), .reset(res));  // open: Qn, preset
endmodule
